# Fritzing sketch Pr_iot (saved by Fritzing 0.9.3b)
breadboards: 1

parts:
  Mod1 = ESP32-TTGO-T-DISPLAY
  R1 = Photocell (LDR) [package=THT]
  R3 = Resistor [tolerance=±5% resistance=1k package=THT]
  C2 = Ceramic Capacitor [capacitance=100nF part_number=103 package="200 mil [THT, multilayer]"]
  R4 = Temperature Sensor (Thermistor) [thermistor_type=NTC package=THT]
  R5 = Resistor [tolerance=±5% resistance=47k package=THT]
  C3 = Ceramic Capacitor [capacitance=1µF part_number=103 package="200 mil [THT, multilayer]"]
  LED1 = smd LED [color="Red (633nm)" package="1206 [SMD]"]
  R6 = Resistor [tolerance=±5% resistance=560 package=THT]
  LED2 = smd LED [color="Green (565nm)" package="1206 [SMD]"]
  R7 = Resistor [tolerance=±5% resistance=560 package=THT]
  LED3 = smd LED [color="Red (633nm)" package="1206 [SMD]"]
  R8 = Resistor [tolerance=±5% resistance=560 package=THT]
  LED4 = smd LED [color="Green (565nm)" package="1206 [SMD]"]
  R9 = Resistor [tolerance=±5% resistance=560 package=THT]

nets:
  N1: Mod1.G-1, Mod1.G-2, Mod1.G-10, Mod1.G-11, Mod1.G-14, R3.Pin_1, C2.1, R5.Pin_1, C3.1, LED1.cathode, LED2.cathode, LED3.cathode, LED4.cathode
  N2: Mod1.2, R8.Pin_1
  N3: Mod1.15, R9.Pin_1
  N4: Mod1.13, R7.Pin_1
  N5: Mod1.12, R6.Pin_1
  N6: Mod1.3V, R1.pin_0, R4.pin_0
  N7: Mod1.39, R4.pin_1, R5.Pin_0, C3.0
  N8: Mod1.36, R1.pin_1, R3.Pin_0, C2.0
  N9: LED1.anode, R6.Pin_0
  N10: LED2.anode, R7.Pin_0
  N11: LED3.anode, R8.Pin_0
  N12: LED4.anode, R9.Pin_0

custom parts:
  ESP32-TTGO-T-DISPLAY: LILYGO TTGO T-Display GD32VF103CBT6 Main Chip ST7789 1.14 Inch IPS 240x135 Resolution Minimalist Development Board.
